# Fritzing sketch Schema (saved by Fritzing 0.9.3b)
breadboards: 2

parts:
  Part1 = Arduino Uno (Rev3)
  U1 = 74HC595 [package="DIP16 [THT]"]
  U2 = 74HC595 [package="DIP16 [THT]"]
  R1 = Resistor [tolerance=±5% resistance=220 package="0805 [SMD]"]
  R2 = Resistor [tolerance=±5% resistance=220 package="0805 [SMD]"]
  R3 = Resistor [tolerance=±5% resistance=220 package="0805 [SMD]"]
  R4 = Resistor [tolerance=±5% resistance=220 package="0805 [SMD]"]
  R5 = Resistor [tolerance=±5% resistance=220 package="0805 [SMD]"]
  R6 = Resistor [tolerance=±5% resistance=220 package="0805 [SMD]"]
  R7 = Resistor [tolerance=±5% resistance=220 package="0805 [SMD]"]
  R0 = Resistor [tolerance=±5% resistance=220 package="0805 [SMD]"]
  Disp2 = LBT2088AH [part_number=LBT2088AH]

nets:
  GND: Part1.GND, U1.GND, U1.OE
  N1: Part1.D2, U2.DS
  N2: Part1.D3_PWM, U1.SH_CP, U2.SH_CP
  N3: Part1.D4, U1.ST_CP, U2.ST_CP
  VCC: Part1.5V, U1.MR, U1.VCC, U2.MR, U2.VCC
  N4: U1.Q1, R1.Pin_1
  N5: U1.Q2, R2.Pin_1
  N6: U1.Q3, R3.Pin_1
  N7: U1.Q4, R4.Pin_1
  N8: U1.Q5, R5.Pin_1
  N9: U1.Q6, R6.Pin_1
  N10: U1.Q7, R7.Pin_1
  N11: U1.DS, U2.Q7'
  N12: U1.Q0, R0.Pin_1
  N13: U2.Q1, Disp2.pin_10
  N14: U2.Q2, Disp2.pin_15
  N15: U2.Q3, Disp2.pin_9
  N16: U2.Q4, Disp2.pin_4
  N17: U2.Q5, Disp2.pin_16
  N18: U2.Q6, Disp2.pin_6
  N19: U2.Q7, Disp2.pin1
  N20: U2.GND, U2.OE
  N21: U2.Q0, Disp2.pin_13
  N22: R1.Pin_0, Disp2.pin_7
  N23: R2.Pin_0, Disp2.pin_3
  N24: R3.Pin_0, Disp2.pin_14
  N25: R4.Pin_0, Disp2.pin2
  N26: R5.Pin_0, Disp2.pin_12
  N27: R6.Pin_0, Disp2.pin_11
  N28: R7.Pin_0, Disp2.pin_5
  N29: R0.Pin_0, Disp2.pin_8
